// Logisim project Q4.circ as structural Verilog: 1 circuit, main circuit main
module main (
  input  A,
  input  B,
  input  C,
  input  D,
  output F
);

  wire and_1_out, and_2_out, and_3_out, and_4_out, and_5_out, and_6_out, and_7_out, and_8_out, and_9_out,
       not_1_out, not_2_out, not_3_out, or_1_out, or_2_out, or_3_out;

  not not_1 (not_1_out, C);
  not not_2 (not_2_out, A);
  not not_3 (not_3_out, B);
  and and_1 (and_1_out, A, B);
  and and_2 (and_2_out, not_2_out, not_3_out);
  and and_3 (and_3_out, and_1_out, not_1_out);
  and and_4 (and_4_out, not_1_out, D);
  and and_5 (and_5_out, and_2_out, and_4_out);
  and and_6 (and_6_out, D, C);
  and and_7 (and_7_out, and_1_out, D);
  and and_8 (and_8_out, and_1_out, and_6_out);
  or or_1 (or_1_out, and_3_out, and_5_out);
  and and_9 (and_9_out, B, and_6_out);
  or or_2 (or_2_out, and_7_out, and_9_out);
  or or_3 (or_3_out, or_2_out, and_8_out);
  or or_4 (F, or_3_out, or_1_out);
endmodule
