// Logisim project 4-bit adder.circ as structural Verilog: 1 circuit, main circuit main
module main (
  input  C,
  input  [3:0] A,
  input  [3:0] B,
  input  in_4,
  input  in_5,
  input  in_6
);

  wire and_1_out, and_2_out, and_3_out, and_4_out, and_5_out, and_6_out, and_7_out, and_8_out, or_1_out,
       or_2_out, or_3_out, xor_1_out, xor_2_out, xor_3_out, xor_4_out;
  wire [0:0] or_4_out;
  wire [3:0] xor_5_out;

  xor xor_1 (xor_1_out, A[0], B[0]);
  xor xor_2 (xor_2_out, A[1], B[1]);
  xor xor_3 (xor_3_out, A[2], B[2]);
  xor xor_4 (xor_4_out, A[3], B[3]);
  xor xor_5 (xor_5_out[0], xor_1_out, C);
  and and_1 (and_1_out, xor_1_out, C);
  and and_2 (and_2_out, B[0], A[0]);
  xor xor_6 (xor_5_out[1], xor_2_out, or_1_out);
  and and_3 (and_3_out, xor_2_out, or_1_out);
  and and_4 (and_4_out, B[1], A[1]);
  xor xor_7 (xor_5_out[2], xor_3_out, or_2_out);
  and and_5 (and_5_out, xor_3_out, or_2_out);
  and and_6 (and_6_out, B[2], A[2]);
  xor xor_8 (xor_5_out[3], xor_4_out, or_3_out);
  and and_7 (and_7_out, xor_4_out, or_3_out);
  and and_8 (and_8_out, B[3], A[3]);
  or or_1 (or_1_out, and_1_out, and_2_out);
  or or_2 (or_2_out, and_3_out, and_4_out);
  or or_3 (or_3_out, and_5_out, and_6_out);
  or or_4 (or_4_out[0], and_7_out, and_8_out);
  Hex_Digit_Display hex_digit_display_1 (.value(xor_5_out));  // open: dp
  Hex_Digit_Display hex_digit_display_2 (.value({in_6, in_5, in_4, or_4_out[0]}));  // open: dp
endmodule
