// Logisim project Decoder.circ as structural Verilog: 2 circuits, main circuit main
module main (
  input  A,
  input  B,
  input  C,
  output S0,
  output S1,
  output S2,
  output S3,
  output S4,
  output S5,
  output S6,
  output S7
);

  wire not_1_out, not_2_out, not_3_out;

  not not_1 (not_1_out, A);
  not not_2 (not_2_out, B);
  not not_3 (not_3_out, C);
  and and_1 (S0, not_3_out, not_2_out, not_1_out);
  and and_2 (S1, C, not_2_out, not_1_out);
  and and_3 (S2, not_3_out, B, not_1_out);
  and and_4 (S3, C, B, not_1_out);
  and and_5 (S4, not_3_out, not_2_out, A);
  and and_6 (S5, C, not_2_out, A);
  and and_7 (S6, not_3_out, B, A);
  and and_8 (S7, C, B, A);
endmodule

module Decode (
  input  in_1,
  input  in_2,
  input  in_3,
  output out_4,
  output out_5,
  output out_6,
  output out_7,
  output out_8,
  output out_9,
  output out_10,
  output out_11
);

  main main_1 (
    .A(in_1), .B(in_2), .C(in_3), .S0(out_4), .S1(out_5), .S2(out_6), .S3(out_7), .S4(out_8), .S5(out_9),
    .S6(out_10), .S7(out_11));
endmodule
