// Logisim project Encoder.circ as structural Verilog: 2 circuits, main circuit main
module main (
  input  I0,
  input  I1,
  input  I2,
  input  I3,
  output A0,
  output A1
);

  or or_1 (A0, I1, I3);
  or or_2 (A1, I2, I3);
endmodule

module Encode (
  input  in_1,
  input  in_2,
  input  in_3,
  input  in_4,
  output out_5,
  output out_6
);

  main main_1 (.I0(in_1), .I1(in_2), .I2(in_3), .I3(in_4), .A0(out_5), .A1(out_6));
endmodule
