// Logisim project Multiplexer.circ as structural Verilog: 2 circuits, main circuit main
module main (
  input  A,
  input  B,
  input  C,
  input  I0,
  input  I1,
  input  I2,
  input  I3,
  input  I4,
  input  I5,
  input  I6,
  input  I7,
  output I
);

  wire and_1_out, and_2_out, and_3_out, and_4_out, and_5_out, and_6_out, and_7_out, and_8_out, not_1_out,
       not_2_out, not_3_out;

  not not_1 (not_1_out, A);
  not not_2 (not_2_out, B);
  not not_3 (not_3_out, C);
  and and_1 (and_1_out, not_3_out, not_2_out, not_1_out, I0);
  and and_2 (and_2_out, C, not_2_out, not_1_out, I1);
  and and_3 (and_3_out, not_3_out, B, not_1_out, I2);
  and and_4 (and_4_out, C, B, not_1_out, I3);
  and and_5 (and_5_out, not_3_out, not_2_out, A, I4);
  and and_6 (and_6_out, C, not_2_out, A, I5);
  and and_7 (and_7_out, not_3_out, B, A, I6);
  and and_8 (and_8_out, C, B, A, I7);
  or or_1 (I, and_1_out, and_2_out, and_3_out, and_4_out, and_5_out, and_6_out, and_7_out, and_8_out);
endmodule

module Multi (
  input  A,
  input  B,
  input  C,
  input  in_4,
  input  in_5,
  input  in_6,
  input  in_7,
  input  in_8,
  input  in_9,
  input  in_10,
  input  in_11,
  output out_12
);

  main main_1 (
    .A(A), .B(B), .C(C), .I0(in_4), .I1(in_5), .I2(in_6), .I3(in_7), .I4(in_8), .I5(in_9), .I6(in_10),
    .I7(in_11), .I(out_12));
endmodule
