// Logisim project Code converters.circ as structural Verilog: 5 circuits, main circuit main
module main (
  input  in_1,
  input  in_2,
  input  in_3,
  input  in_4,
  input  in_5,
  input  in_6,
  input  in_7,
  input  in_8
);

  wire [3:0] btog_1_g0, gtob_1_b0;

  BtoG btog_1 (
    .B3(in_1), .B2(in_2), .B1(in_3), .B0(in_4), .G3(btog_1_g0[3]), .G2(btog_1_g0[2]), .G1(btog_1_g0[1]),
    .G0(btog_1_g0[0]));
  GtoB gtob_1 (
    .G3(in_5), .G2(in_6), .G1(in_7), .G0(in_8), .B3(gtob_1_b0[3]), .B2(gtob_1_b0[2]), .B1(gtob_1_b0[1]),
    .B0(gtob_1_b0[0]));
  Hex_Digit_Display hex_digit_display_1 (.value(btog_1_g0));  // open: dp
  Hex_Digit_Display hex_digit_display_2 (.value(gtob_1_b0));  // open: dp
endmodule

module BtoG (
  input  B3,
  input  B2,
  input  B1,
  input  B0,
  output G3,
  output G2,
  output G1,
  output G0
);

  xor xor_1 (G2, B3, B2);
  xor xor_2 (G1, B2, B1);
  xor xor_3 (G0, B1, B0);

  assign G3 = B3;
endmodule

module GtoB (
  input  G3,
  input  G2,
  input  G1,
  input  G0,
  output B3,
  output B2,
  output B1,
  output B0
);

  xor xor_1 (B2, G3, G2);
  xor xor_2 (B1, B2, G1);
  xor xor_3 (B0, B1, G0);

  assign B3 = G3;
endmodule

module Fadder (
  input  in_1,
  input  A0,
  input  A1,
  input  A2,
  input  A3,
  input  B0,
  input  B1,
  input  B2,
  input  B3,
  output S0,
  output S1,
  output S2,
  output S3,
  output Cout
);

  wire and_1_out, and_2_out, and_3_out, and_4_out, and_5_out, and_6_out, and_7_out, and_8_out, or_1_out,
       or_2_out, or_3_out, xor_1_out, xor_2_out, xor_3_out, xor_4_out;

  xor xor_1 (xor_1_out, A0, B0);
  xor xor_2 (xor_2_out, A1, B1);
  xor xor_3 (xor_3_out, A2, B2);
  xor xor_4 (xor_4_out, A3, B3);
  xor xor_5 (S0, xor_1_out, in_1);
  and and_1 (and_1_out, xor_1_out, in_1);
  and and_2 (and_2_out, B0, A0);
  xor xor_6 (S1, xor_2_out, or_1_out);
  and and_3 (and_3_out, xor_2_out, or_1_out);
  and and_4 (and_4_out, B1, A1);
  xor xor_7 (S2, xor_3_out, or_2_out);
  and and_5 (and_5_out, xor_3_out, or_2_out);
  and and_6 (and_6_out, B2, A2);
  xor xor_8 (S3, xor_4_out, or_3_out);
  and and_7 (and_7_out, xor_4_out, or_3_out);
  and and_8 (and_8_out, B3, A3);
  or or_1 (or_1_out, and_1_out, and_2_out);
  or or_2 (or_2_out, and_3_out, and_4_out);
  or or_3 (or_3_out, and_5_out, and_6_out);
  or or_4 (Cout, and_7_out, and_8_out);
endmodule

module BCDadder (
  input  in_1,
  input  in_2,
  input  in_3,
  input  in_4,
  input  in_5,
  input  in_6,
  input  in_7,
  input  in_8,
  input  in_9,
  input  in_10,
  input  in_11,
  input  in_12,
  input  in_13,
  input  in_14
);

  wire and_1_out, and_2_out, fadder_1_cout, fadder_1_s0, fadder_1_s1, fadder_1_s2, fadder_1_s3, or_1_out,
       undriven;
  wire [0:0] or_2_out;
  wire [3:0] fadder_2_s0;

  Fadder fadder_1 (
    .in_1(in_1), .A0(in_3), .A1(in_4), .A2(in_5), .A3(in_7), .B0(in_8), .B1(in_9), .B2(in_10), .B3(in_11),
    .S0(fadder_1_s0), .S1(fadder_1_s1), .S2(fadder_1_s2), .S3(fadder_1_s3), .Cout(fadder_1_cout));
  and and_1 (and_1_out, fadder_1_s2, fadder_1_s3);
  and and_2 (and_2_out, fadder_1_s1, fadder_1_s3);
  or or_1 (or_1_out, fadder_1_cout, and_2_out);
  or or_2 (or_2_out[0], or_1_out, and_1_out);
  Fadder fadder_2 (
    .in_1(undriven), .A0(fadder_1_s0), .A1(fadder_1_s1), .A2(fadder_1_s2), .A3(fadder_1_s3), .B0(in_2),
    .B1(or_2_out[0]), .B2(or_2_out[0]), .B3(in_6), .S0(fadder_2_s0[0]), .S1(fadder_2_s0[1]),
    .S2(fadder_2_s0[2]), .S3(fadder_2_s0[3]));  // open: Cout
  Hex_Digit_Display hex_digit_display_1 (.value(fadder_2_s0));  // open: dp
  Hex_Digit_Display hex_digit_display_2 (.value({in_14, in_13, in_12, or_2_out[0]}));  // open: dp
endmodule
