// Logisim project downCountercountingtwice.circ as structural Verilog: 1 circuit, main circuit main
module main (
  input  in_1,
  input  in_2,
  input  in_3,
  input  in_4,
  input  in_5
);

  wire and_1_out, and_2_out, and_3_out, and_4_out, and_5_out, and_6_out, and_7_out, and_8_out, and_9_out,
       and_10_out, clock_1_out, clock_2_out, j_k_ff_1_qn, j_k_ff_3_qn, not_1_out, not_2_out, or_1_out;
  wire [2:0] j_k_ff_1_q;
  wire [3:0] j_k_ff_2_q;

  Clock clock_1 (.out(clock_1_out));
  Clock clock_2 (.out(clock_2_out));
  or or_1 (or_1_out, and_1_out, and_3_out);
  J_K_Flip_Flop j_k_ff_1 (
    .J(in_2), .K(in_2), .clk(clock_2_out), .Q(j_k_ff_1_q[0]), .Qn(j_k_ff_1_qn), .preset(in_1), .reset(in_3));
  not not_1 (not_1_out, j_k_ff_1_q[0]);
  and and_1 (and_1_out, not_1_out, not_2_out, j_k_ff_1_q[2]);
  not not_2 (not_2_out, j_k_ff_1_q[1]);
  J_K_Flip_Flop j_k_ff_2 (
    .J(or_1_out), .K(or_1_out), .clk(clock_1_out), .Q(j_k_ff_2_q[0]), .reset(in_5));  // open: Qn, preset
  and and_2 (and_2_out, in_2, j_k_ff_1_qn);
  and and_3 (and_3_out, j_k_ff_1_q[0], j_k_ff_1_q[1], j_k_ff_1_q[2]);
  and and_4 (and_4_out, or_1_out, j_k_ff_2_q[0]);
  J_K_Flip_Flop j_k_ff_3 (
    .J(and_2_out), .K(and_2_out), .clk(clock_2_out), .Q(j_k_ff_1_q[1]), .Qn(j_k_ff_3_qn), .preset(in_1),
    .reset(in_3));
  J_K_Flip_Flop j_k_ff_4 (
    .J(and_4_out), .K(and_4_out), .clk(clock_1_out), .Q(j_k_ff_2_q[1]), .reset(in_5));  // open: Qn, preset
  and and_5 (and_5_out, in_2, and_6_out);
  and and_6 (and_6_out, and_2_out, j_k_ff_3_qn);
  J_K_Flip_Flop j_k_ff_5 (
    .J(and_5_out), .K(and_5_out), .clk(clock_2_out), .Q(j_k_ff_1_q[2]), .preset(in_1), .reset(in_3));  // open: Qn
  and and_7 (and_7_out, or_1_out, and_8_out);
  and and_8 (and_8_out, and_4_out, j_k_ff_2_q[1]);
  J_K_Flip_Flop j_k_ff_6 (
    .J(and_7_out), .K(and_7_out), .clk(clock_1_out), .Q(j_k_ff_2_q[2]), .reset(in_5));  // open: Qn, preset
  and and_9 (and_9_out, and_7_out, j_k_ff_2_q[2]);
  and and_10 (and_10_out, or_1_out, and_9_out);
  J_K_Flip_Flop j_k_ff_7 (
    .J(and_10_out), .K(and_10_out), .clk(clock_1_out), .Q(j_k_ff_2_q[3]), .reset(in_5));  // open: Qn, preset
  Hex_Digit_Display hex_digit_display_1 (.value({in_4, j_k_ff_1_q}));  // open: dp
  Hex_Digit_Display hex_digit_display_2 (.value(j_k_ff_2_q));  // open: dp
endmodule
