// Logisim project stopwatch.circ as structural Verilog: 2 circuits, main circuit main
module main (
  input  in_1,
  input  in_2,
  input  in_3
);

  wire and_1_out, and_2_out, and_3_out, and_4_out, and_5_out, and_6_out, and_7_out, clock_1_out, not_1_out,
       not_2_out, not_3_out, not_4_out, not_5_out, not_6_out, not_7_out, t_ff_4_q, t_ff_5_q, t_ff_6_q;
  wire [2:0] t_ff_1_q;
  wire [3:0] t_ff_4_qn;

  Clock clock_1 (.out(clock_1_out));
  not not_1 (not_1_out, in_1);
  not not_2 (not_2_out, t_ff_1_q[0]);
  T_Flip_Flop t_ff_1 (.T(not_1_out), .clk(clock_1_out), .Q(t_ff_1_q[0]), .reset(in_3));  // open: Qn, preset
  and and_1 (and_1_out, not_1_out, not_2_out);
  T_Flip_Flop t_ff_2 (.T(and_1_out), .clk(clock_1_out), .Q(t_ff_1_q[1]), .reset(in_3));  // open: Qn, preset
  not not_3 (not_3_out, t_ff_1_q[1]);
  not not_4 (not_4_out, t_ff_1_q[0]);
  and and_2 (and_2_out, and_4_out, not_1_out);
  and and_3 (and_3_out, and_1_out, not_3_out);
  T_Flip_Flop t_ff_3 (.T(and_3_out), .clk(clock_1_out), .Q(t_ff_1_q[2]), .reset(in_3));  // open: Qn, preset
  and and_4 (and_4_out, not_4_out, t_ff_1_q[1], t_ff_1_q[2]);
  T_Flip_Flop t_ff_4 (.T(and_2_out), .clk(clock_1_out), .Q(t_ff_4_q), .Qn(t_ff_4_qn[0]), .reset(in_3));  // open: preset
  not not_5 (not_5_out, t_ff_4_q);
  Hex_Digit_Display hex_digit_display_1 (.value({in_2, t_ff_1_q}));  // open: dp
  and and_5 (and_5_out, and_2_out, not_5_out);
  Hex_Digit_Display hex_digit_display_2 (.value(t_ff_4_qn));  // open: dp
  not not_6 (not_6_out, t_ff_5_q);
  T_Flip_Flop t_ff_5 (.T(and_5_out), .clk(clock_1_out), .Q(t_ff_5_q), .Qn(t_ff_4_qn[1]), .reset(in_3));  // open: preset
  and and_6 (and_6_out, and_5_out, not_6_out);
  not not_7 (not_7_out, t_ff_6_q);
  T_Flip_Flop t_ff_6 (.T(and_6_out), .clk(clock_1_out), .Q(t_ff_6_q), .Qn(t_ff_4_qn[2]), .reset(in_3));  // open: preset
  and and_7 (and_7_out, and_6_out, not_7_out);
  T_Flip_Flop t_ff_7 (.T(and_7_out), .clk(clock_1_out), .Qn(t_ff_4_qn[3]), .reset(in_3));  // open: Q, preset
endmodule

module q2 (
  input  in_1,
  input  in_2,
  input  in_3
);

  wire and_1_out, and_2_out, and_3_out, and_4_out, and_5_out, and_6_out, and_7_out, clock_1_out, nor_1_out,
       not_1_out, not_2_out, not_3_out, not_4_out, not_5_out, not_6_out, not_7_out, not_8_out, or_1_out,
       t_ff_4_q, t_ff_5_q, t_ff_6_q;
  wire [2:0] t_ff_1_q;
  wire [3:0] t_ff_4_qn;

  Clock clock_1 (.out(clock_1_out));
  not not_1 (not_1_out, in_1);
  not not_2 (not_2_out, t_ff_1_q[0]);
  T_Flip_Flop t_ff_1 (.T(not_1_out), .clk(clock_1_out), .Q(t_ff_1_q[0]), .reset(in_3));  // open: Qn, preset
  and and_1 (and_1_out, not_1_out, not_2_out);
  T_Flip_Flop t_ff_2 (.T(and_1_out), .clk(clock_1_out), .Q(t_ff_1_q[1]), .reset(in_3));  // open: Qn, preset
  not not_3 (not_3_out, t_ff_1_q[1]);
  not not_4 (not_4_out, t_ff_1_q[0]);
  nor nor_1 (nor_1_out, t_ff_1_q[2], t_ff_1_q[1], t_ff_1_q[0]);
  and and_2 (and_2_out, or_1_out, not_1_out);
  and and_3 (and_3_out, and_1_out, not_3_out);
  or or_1 (or_1_out, nor_1_out, and_4_out);
  T_Flip_Flop t_ff_3 (.T(and_3_out), .clk(clock_1_out), .Q(t_ff_1_q[2]), .reset(in_3));  // open: Qn, preset
  not not_5 (not_5_out, t_ff_1_q[1]);
  and and_4 (and_4_out, not_4_out, not_5_out, t_ff_1_q[2]);
  T_Flip_Flop t_ff_4 (.T(and_2_out), .clk(clock_1_out), .Q(t_ff_4_q), .Qn(t_ff_4_qn[0]), .reset(in_3));  // open: preset
  not not_6 (not_6_out, t_ff_4_q);
  Hex_Digit_Display hex_digit_display_1 (.value({in_2, t_ff_1_q}));  // open: dp
  and and_5 (and_5_out, and_2_out, not_6_out);
  Hex_Digit_Display hex_digit_display_2 (.value(t_ff_4_qn));  // open: dp
  not not_7 (not_7_out, t_ff_5_q);
  T_Flip_Flop t_ff_5 (.T(and_5_out), .clk(clock_1_out), .Q(t_ff_5_q), .Qn(t_ff_4_qn[1]), .reset(in_3));  // open: preset
  and and_6 (and_6_out, and_5_out, not_7_out);
  not not_8 (not_8_out, t_ff_6_q);
  T_Flip_Flop t_ff_6 (.T(and_6_out), .clk(clock_1_out), .Q(t_ff_6_q), .Qn(t_ff_4_qn[2]), .reset(in_3));  // open: preset
  and and_7 (and_7_out, and_6_out, not_8_out);
  T_Flip_Flop t_ff_7 (.T(and_7_out), .clk(clock_1_out), .Qn(t_ff_4_qn[3]), .reset(in_3));  // open: Q, preset
endmodule
